# Fritzing sketch smart door open and close (saved by Fritzing 0.9.3b)
breadboards: 1

parts:
  J1 = Basic Servo
  J2 = Basic Servo
  hc-sr1 = hc-sr04
  Part1 = Arduino Uno (Rev3)
  LED1 = LED - 3mm [color="Red (633nm)" package="3 mm [THT]"]
  R1 = Resistor [tolerance=±5% resistance=2k package=THT]
  R2 = Resistor [tolerance=±5% resistance=2k package=THT]
  J3 = Piezo Speaker

nets:
  GND: J1.gnd, J2.gnd, hc-sr1.GND, Part1.GND, LED1.cathode, J3.pin1
  VCC: J1.vcc, J2.vcc, hc-sr1.VCC, Part1.5V
  N1: J1.pulse, J2.pulse, Part1.D11_PWM/MOSI
  N2: hc-sr1.Trig, Part1.D5_PWM
  N3: hc-sr1.Echo, Part1.D6_PWM
  N4: Part1.D2, R2.Pin_1
  N5: Part1.D3_PWM, R1.Pin_1
  N6: LED1.anode, R1.Pin_0
  N7: R2.Pin_0, J3.pin2

// code stored in the sketch: door.ino
#include<Servo.h>
Servo myservo;
int pos=20;
const int trigpin=5;
const int echopin=6;
const int led1=2;
const int buzzer=3;

long duration;
float distance;


void setup()
{
  myservo.attach(11);
  pinMode(trigpin,OUTPUT);
  pinMode(echopin,INPUT);
  pinMode(led1,OUTPUT);
  pinMode(buzzer,OUTPUT);
  

  myservo.write(pos);
  
  
}
void loop()
{
  //serial.begin(9600);
  digitalWrite(trigpin,LOW);
  delayMicroseconds(2);
  digitalWrite(trigpin,HIGH);
  delayMicroseconds(10);
  digitalWrite(trigpin,LOW);

  duration=pulseIn(echopin,HIGH);
  distance=0.034*(duration/2);
  //serial.println(distance);
  if(distance<35)
  {
    digitalWrite(led1,HIGH);
    digitalWrite(buzzer,HIGH);
    delay(500);
  }
  else
  {
     digitalWrite(led1,LOW);
     digitalWrite(buzzer,LOW);
     delay(400);
  }
  if(distance<27)
  {
    myservo.write(pos+160);
    delay(1000);
    
  }
  else
  {
    myservo.write(pos);
    
  }
  delay(300);
}
